# Fritzing sketch BalanceBotWiring (saved by Fritzing 0.9.3b)
breadboards: 1

parts:
  Part1 = Arduino Nano (Rev3.0) (ICSP)
  Part2 = Bluetooth HC-05 Macho
  Part3 = Motor Driver 1A Dual TB6612FNG
  DC_Mot_Enc1 = DC Motor with two-phase hall-encoder [part_number=VT-E-G25A-06-177E]
  DC_Mot_Enc2 = DC Motor with two-phase hall-encoder [part_number=VT-E-G25A-06-177E]
  U1 = LIPO-110mAh [package=lipo-110]
  U2 = LIPO-110mAh [package=lipo-110]
  Part5 = InvenSense MPU6050
  S1 = Toggle Switch [package=THT]
  S2 = Toggle Switch [package=THT]
  C1 = Capacitor [package=cap-pth-5mm]
  R1 = Resistor [tolerance=±5% resistance=220 package="0402 [SMD]"]

nets:
  N1: Part1.D1/TX, Part2.RXD
  N2: Part1.D0/RX, Part2.TXD
  N3: Part1.RESET, C1.1, R1.Pin_1
  GND: Part1.GND, Part2.GND, Part3.GND, DC_Mot_Enc1.pin6, DC_Mot_Enc2.pin6, U2.-, Part5.GND, R1.Pin_0
  N4: Part1.D2, Part5.INT
  N5: Part1.D5, Part3.AIN2
  N6: Part1.D6, Part3.AIN1
  N7: Part1.D7, Part3.BIN1
  N8: Part1.D8, Part3.BIN2
  N9: Part1.D9, Part3.PWMB
  N10: Part1.D10, Part3.PWMA
  N11: Part1.VIN, S1.L1
  VCC: Part1.5V, Part2.VCC, DC_Mot_Enc1.pin3, DC_Mot_Enc2.pin3, Part5.VCC
  N12: Part1.A5, Part5.SCL
  N13: Part1.A4, Part5.SDA
  N14: Part1.A3, DC_Mot_Enc1.pin5
  N15: Part1.A2, DC_Mot_Enc1.pin4
  N16: Part1.A1, DC_Mot_Enc2.pin5
  N17: Part1.A0, DC_Mot_Enc2.pin4
  N18: Part2.State, C1.2
  N19: Part3.B01, DC_Mot_Enc2.pin1
  N20: Part3.B02, DC_Mot_Enc2.pin2
  N21: Part3.A02, DC_Mot_Enc1.pin1
  N22: Part3.A01, DC_Mot_Enc1.pin2
  N23: Part3.VM, S1.COM, S2.COM
  N24: U1.+, S2.L1
  N25: U1.-, U2.+
